# Fritzing sketch wiring_sketch (saved by Fritzing 0.9.3b)
breadboards: 1

parts:
  LED1 = smd LED [color="Red (633nm)" package="0603 [SMD]"]
  LED2 = smd LED [color="Green (570nm)" package="0603 [SMD]"]
  R1 = Resistor [tolerance=±5% resistance=220 package=THT]
  R2 = Resistor [tolerance=±5% resistance=220 package=THT]
  Power_Supply = YwRobot Breadboard Power Supply [part_number=545043]
  UHF_RFID_5P1 = Generic UHF RFID 5-Pin UART Module
  ESP32 = ESP 32 DEVKIT DOIT

nets:
  N1: LED1.cathode, R1.Pin_1
  N2: LED1.anode, LED2.anode, UHF_RFID_5P1.TX, UHF_RFID_5P1.RX, ESP32.D22, ESP32.RX2, ESP32.D4, ESP32.D2, ESP32.D15
  N3: LED2.cathode, R2.Pin_1
  VCC: Power_Supply.VCC, UHF_RFID_5P1.VCC, ESP32.Vin
  GND: Power_Supply.GND, UHF_RFID_5P1.GND
  N4: UHF_RFID_5P1.EN, ESP32.D12

custom parts:
  YwRobot Breadboard Power Supply: The YwRobot Breadboard Power Supply (MB-V2) has two power rails; they can be 5V or 3V3. Power to the module can be provided through the female USB socket or through the A10 (female) 2.1mm power jack.
  Generic UHF RFID 5-Pin UART Module: Generic 5-pin UHF RFID module for Fritzing 0.9.3b. Pins: VCC, GND, TX, RX, EN.
